# Fritzing sketch dashboard-led-button (saved by Fritzing 0.9.3b)
breadboards: 1

parts:
  S1 = Pushbutton [package="[THT]"]
  R1 = Resistor [tolerance=±5% resistance=220 package="0402 [SMD]"]
  LED1 = LED - 5mm [color="Red (633nm)" package="5 mm [THT]"]
  Raspberry_Pi_1 = Raspberry Pi 3 [part_number=RPI-3-V1.2]

nets:
  N1: S1.Pin_1, S1.Pin_2, Raspberry_Pi_1.GIPO24
  N2: S1.Pin_3, S1.Pin_4, Raspberry_Pi_1.3v3
  N3: R1.Pin_0, Raspberry_Pi_1.GIPO22
  N4: R1.Pin_1, LED1.anode
