# Fritzing sketch lcd (saved by Fritzing 0.9.3b)
breadboards: 1

parts:
  Raspberry_Pi_1 = Raspberry Pi 3 [part_number=RPI-3-V1.2]
  LCD1 = LCD screen

nets (from the breadboard view):
  3V3: Raspberry_Pi_1.3v3, Raspberry_Pi_1.3V3, LCD1.LED+
  N1: Raspberry_Pi_1.GIPO17, LCD1.DB4
  GND: Raspberry_Pi_1.GIPO27, Raspberry_Pi_1.GIPO10, Raspberry_Pi_1.GND, LCD1.VSS, LCD1.R/W, LCD1.E, LCD1.DB6, LCD1.LED-
  N2: Raspberry_Pi_1.GIPO7, LCD1.RS
  N3: Raspberry_Pi_1.GIPO23, LCD1.DB7
  N4: Raspberry_Pi_1.GIPO18, LCD1.DB5
  5V: Raspberry_Pi_1.5V, LCD1.VDD
